# Fritzing sketch Phone Circuit (saved by Fritzing 0.9.2b)
breadboards: 1

parts:
  VCC1 = Battery block 9V
  U5 = 3.5mm Audio Jack [package=audio-jack]
  LED2 = smd LED [color="Red (633nm)" package="0805 [SMD]"]
  LED4 = smd LED [color="Red (633nm)" package="0805 [SMD]"]
  LED5 = smd LED [color="Red (633nm)" package="0805 [SMD]"]
  LED6 = smd LED [color="Red (633nm)" package="0805 [SMD]"]
  LED7 = smd LED [color="Red (633nm)" package="0805 [SMD]"]
  LED8 = smd LED [color="Red (633nm)" package="0805 [SMD]"]
  LED9 = smd LED [color="Red (633nm)" package="0805 [SMD]"]
  LED10 = smd LED [color="Red (633nm)" package="0805 [SMD]"]
  R3 = Resistor [tolerance=±5% resistance=220 package="2010 [SMD]"]
  R4 = Resistor [tolerance=±5% resistance=220 package="2010 [SMD]"]
  R5 = Resistor [tolerance=±5% resistance=220 package="2010 [SMD]"]
  R6 = Resistor [tolerance=±5% resistance=220 package="2010 [SMD]"]
  R7 = Resistor [tolerance=±5% resistance=220 package="2010 [SMD]"]
  R8 = Resistor [tolerance=±5% resistance=220 package="2010 [SMD]"]
  R9 = Resistor [tolerance=±5% resistance=220 package="2010 [SMD]"]
  R10 = Resistor [tolerance=±5% resistance=220 package="2010 [SMD]"]

nets:
  N1: VCC1.-, U5.RIGHT, U5.SLEEVE
  N2: VCC1.+, R3.Pin_0, R4.Pin_0, R5.Pin_0, R6.Pin_0, R7.Pin_0, R8.Pin_0, R9.Pin_0, R10.Pin_0
  N3: U5.LEFT, LED2.cathode, LED4.cathode, LED5.cathode, LED6.cathode, LED7.cathode, LED8.cathode, LED9.cathode, LED10.cathode
  N4: LED2.anode, R5.Pin_1
  N5: LED4.anode, R9.Pin_1
  N6: LED5.anode, R10.Pin_1
  N7: LED6.anode, R8.Pin_1
  N8: LED7.anode, R7.Pin_1
  N9: LED8.anode, R6.Pin_1
  N10: LED9.anode, R4.Pin_1
  N11: LED10.anode, R3.Pin_1

notes:
  Smart Phone goes here. Insert the Audio jack into the phone.
  Connect left and right of audio jack to GND of 9V battery.
  Left
  Right
